# Fritzing sketch Ex_3_0_ReadingAndWriting (saved by Fritzing 0.9.2b)
breadboards: 1

parts:
  R4 = TRIMPOT [package=3386u]
  LED1 = smd LED [color="Red (633nm)" package="0805 [SMD]"]
  Part1 = Arduino Due (Rev2b)

nets:
  N1: R4.WIPER, LED1.cathode
  N2: R4.CW, Part1.IOREF
  N3: LED1.anode, Part1.GND
